// Logisim project project.circ as structural Verilog
module main (
);

  wire ADD_R0, ADD_R1, address_1_out, alu_a6_1_negative, alu_a6_1_out0, alu_a6_1_out1, alu_a6_1_out2,
       alu_a6_1_out3, alu_a6_1_overflow, alu_a6_1_zero, and_1_out, and_2_out, and_3_out, and_4_out,
       and_5_out, and_6_out, and_7_out, and_8_out, and_9_out, and_10_out, and_11_out, and_12_out, and_13_out,
       and_14_out, and_15_out, and_16_out, and_17_out, and_18_out, and_19_out, and_20_out, ar_1_ar_out_0,
       ar_1_ar_out_1, ar_1_ar_out_2, arithmic, clock_1_out, CU0, CU0_2, CU1, CU1_2, CU2, CU2_2, CU3, CU3_2,
       CU4, CU4_2, CU5, CU5_2, CU6, CU6_2, CU7, CU7_2, CU8, CU8_2, CU9, CU9_2, data_out_1_data_out_0,
       data_out_1_data_out_1, data_out_1_data_out_2, data_out_1_data_out_3, data_out_2_data_out_0,
       data_out_2_data_out_1, data_out_2_data_out_2, data_out_2_data_out_3, data_out_3_data_out_0,
       data_out_3_data_out_1, data_out_3_data_out_2, data_out_3_data_out_3, display_1_out_12,
       display_1_reg_1, display_1_reg_2, display_1_reg_3, display_1_reg_4, display_1_reg_5, display_1_reg_6,
       display_1_reg_7, dr_1_dr_0, dr_1_dr_1, dr_1_dr_2, dr_1_dr_3, fecth_add_bit0_out, fecth_add_bit1_out,
       fecth_add_bit2_out, FETCH, HALT, increamenter_1_inc_out_0, increamenter_1_inc_out_1,
       increamenter_1_inc_out_2, ir_1_ir_out_0, ir_1_ir_out_1, ir_1_ir_out_2, ir_1_ir_out_3, LEFT_r0_out_0,
       LEFT_r0_out_1, LEFT_r0_out_2, LEFT_r0_out_3, load, load_data_1_bit0_out, load_data_1_bit1_out,
       load_data_1_bit2_out, load_data_1_bit3_out, load_data_2_bit0_out, load_data_2_bit1_out,
       load_data_2_bit2_out, load_data_2_bit3_out, load_R0_0, load_R0_1, load_R1_0, load_R1_1,
       mar_1_mar_out_0, mar_1_mar_out_1, mar_1_mar_out_2, MBR_0, MBR_1, mbr_1_mbr_out_0, mbr_1_mbr_out_1,
       mbr_1_mbr_out_2, mbr_1_mbr_out_3, MBR_2, MBR_3, merge_1_out_0, merge_1_out_1, merge_1_out_2,
       merge_1_out_3, merge_2_out_0, merge_2_out_1, merge_2_out_2, merge_2_out_3, merge_3_out_0,
       merge_3_out_1, merge_3_out_2, merge_3_out_3, merge_4_out_0, merge_4_out_1, merge_4_out_2,
       merge_4_out_3, merge_5_out_0, merge_5_out_1, merge_5_out_2, merge_5_out_3, merge_6_out_0,
       merge_6_out_1, merge_6_out_2, merge_6_out_3, merge_7_out_0, merge_7_out_1, merge_7_out_2,
       merge_8_out_0, merge_8_out_1, merge_8_out_2, merge_8_out_3, mode_1_mode_out, not_1_out, not_2_out,
       or_1_out, or_2_out, or_3_out, or_4_out, or_5_out, or_6_out, or_7_out, or_8_out, or_9_out, or_10_out,
       or_11_out, or_12_out, or_13_out, or_14_out, or_15_out, or_16_out, or_17_out, or_18_out, or_19_out,
       or_20_out, or_21_out, or_22_out, or_23_out, or_24_out, or_25_out, or_26_out, or_27_out, or_28_out,
       or_29_out, or_30_out, or_31_out, or_33_out, or_34_out, or_35_out, or_37_out, or_38_out, or_39_out,
       or_40_out, or_41_out, or_44_out, or_45_out, or_46_out, pc_1_pc_out_0, pc_1_pc_out_1, pc_1_pc_out_2,
       RAM_0_0, RAM_0_1, RAM_0_2, RAM_0_3, ram_a5_1_output0, ram_a5_1_output1, ram_a5_1_output2,
       ram_a5_1_output3, register_0_1_r0_out_0, register_0_1_r0_out_1, register_0_1_r0_out_2,
       register_0_1_r0_out_3, register_0_2_r0_out_0, register_0_2_r0_out_1, register_0_2_r0_out_2,
       register_0_2_r0_out_3, register_1_1_r1_out_0, register_1_1_r1_out_1, register_1_1_r1_out_2,
       register_1_1_r1_out_3, Right_r0_out_0, Right_r0_out_1, Right_r0_out_2, Right_r0_out_3,
       save_data_1_bit0_out, save_data_1_bit1_out, save_data_1_bit2_out, save_data_1_bit3_out,
       save_data_2_bit0_out, save_data_2_bit1_out, save_data_2_bit2_out, save_data_2_bit3_out, save_R0_0,
       save_R0_1, save_R1_0, save_R1_1, selector_3bits_1_bit0_out, selector_3bits_1_bit1_out,
       selector_3bits_1_bit2_out, selector_4bit_1_bit0_out, selector_4bit_1_bit1_out,
       selector_4bit_1_bit2_out, selector_4bit_1_bit3_out, selector_4bit_3_bit0_out,
       selector_4bit_3_bit1_out, selector_4bit_3_bit2_out, selector_4bit_3_bit3_out, SUB_R0, SUB_R1,
       undriven, undriven_2, undriven_3, undriven_4, write;

  and and_1 (and_1_out, CU9_2, write);
  or or_1 (or_1_out, CU2, or_6_out, CU2_2);
  selector_4bit load_data_1 (
    .bit_3(ram_a5_1_output3), .bit2(ram_a5_1_output2), .bit1(ram_a5_1_output1), .bit0(ram_a5_1_output0),
    .CU_in(or_1_out), .bit2_out(load_data_1_bit2_out), .bit1_out(load_data_1_bit1_out),
    .bit0_out(load_data_1_bit0_out), .bit3_out(load_data_1_bit3_out));
  and and_2 (and_2_out, CU7_2, load);
  and and_3 (and_3_out, write, CU8_2);
  or or_2 (or_2_out, CU2, CU2_2, and_1_out, and_4_out);
  or or_3 (or_3_out, CU2_2, and_2_out, and_3_out);
  or or_4 (or_4_out, CU6_2, CU0);
  merge merge_1 (
    .in_1_3(load_data_1_bit3_out), .in_1_2(load_data_1_bit2_out), .in_1_1(load_data_1_bit1_out),
    .in_1_0(load_data_1_bit0_out), .in_2_3(save_data_1_bit3_out), .in_2_2(save_data_1_bit2_out),
    .in_2_1(save_data_1_bit1_out), .in_2_0(save_data_1_bit0_out), .out_0(merge_1_out_0),
    .out_3(merge_1_out_3), .out_2(merge_1_out_2), .out_1(merge_1_out_1));
  or or_5 (or_5_out, CU1_2, CU6_2);
  and and_4 (and_4_out, or_6_out, load);
  RAM_A5 ram_a5_1 (
    .CLOCK_RAM(or_2_out), .add2(ar_1_ar_out_2), .add1(ar_1_ar_out_1), .add0(ar_1_ar_out_0),
    .mode(mode_1_mode_out), .data3(save_data_2_bit3_out), .data2(save_data_2_bit2_out),
    .data1(save_data_2_bit1_out), .data0(save_data_2_bit0_out), .output3(ram_a5_1_output3),
    .output2(ram_a5_1_output2), .output1(ram_a5_1_output1), .output0(ram_a5_1_output0), .RAM_0_3(RAM_0_3),
    .RAM_0_2(RAM_0_2), .RAM_0_1(RAM_0_1), .RAM_0_0(RAM_0_0));
  AR ar_1 (
    .AR_IN_2(fecth_add_bit2_out), .AR_IN_1(fecth_add_bit1_out), .AR_IN_0(fecth_add_bit0_out),
    .CLOCK_AR(or_5_out), .AR_out_2(ar_1_ar_out_2), .AR_out_1(ar_1_ar_out_1), .AR_out_0(ar_1_ar_out_0));
  selector_4bit save_data_2 (
    .bit_3(dr_1_dr_3), .bit2(dr_1_dr_2), .bit1(dr_1_dr_1), .bit0(dr_1_dr_0), .CU_in(and_5_out),
    .bit2_out(save_data_2_bit2_out), .bit1_out(save_data_2_bit1_out), .bit0_out(save_data_2_bit0_out),
    .bit3_out(save_data_2_bit3_out));
  DR dr_1 (
    .DR_IN_3(merge_1_out_3), .DR_IN_2(merge_1_out_2), .DR_IN_1(merge_1_out_1), .DR_IN_0(merge_1_out_0),
    .CLOCK_DR(or_3_out), .DR_3(dr_1_dr_3), .DR_2(dr_1_dr_2), .DR_1(dr_1_dr_1), .DR_0(dr_1_dr_0));
  MODE mode_1 (.MODE_IN(or_15_out), .CLOCK_MODE(or_4_out), .MODE_OUT(mode_1_mode_out));
  selector_4bit save_data_1 (
    .bit_3(MBR_3), .bit2(MBR_2), .bit1(MBR_1), .bit0(MBR_0), .CU_in(and_6_out),
    .bit2_out(save_data_1_bit2_out), .bit1_out(save_data_1_bit1_out), .bit0_out(save_data_1_bit0_out),
    .bit3_out(save_data_1_bit3_out));
  or or_6 (or_6_out, CU7_2, CU7);
  or or_7 (or_7_out, CU3, CU3_2);
  or or_8 (or_8_out, CU9, CU9_2);
  and and_5 (and_5_out, or_8_out, write);
  and and_6 (and_6_out, write, or_11_out);
  or or_9 (or_9_out, write, load);
  or or_10 (or_10_out, CU6_2, CU6);
  selector_4bit load_data_2 (
    .bit_3(dr_1_dr_3), .bit2(dr_1_dr_2), .bit1(dr_1_dr_1), .bit0(dr_1_dr_0), .CU_in(or_13_out),
    .bit2_out(load_data_2_bit2_out), .bit1_out(load_data_2_bit1_out), .bit0_out(load_data_2_bit0_out),
    .bit3_out(load_data_2_bit3_out));
  or or_11 (or_11_out, CU8, CU8_2);
  and and_7 (and_7_out, or_9_out, or_10_out);
  or or_12 (or_12_out, CU8_2, CU8);
  and and_8 (and_8_out, or_12_out, load);
  or or_13 (or_13_out, or_7_out, and_8_out);
  or or_14 (or_14_out, CU1, CU1_2, and_7_out);
  merge merge_2 (
    .in_1_3(undriven), .in_1_2(merge_3_out_2), .in_1_1(merge_3_out_1), .in_1_0(merge_3_out_0),
    .in_2_3(load_data_2_bit3_out), .in_2_2(load_data_2_bit2_out), .in_2_1(load_data_2_bit1_out),
    .in_2_0(load_data_2_bit0_out), .out_0(merge_2_out_0), .out_3(merge_2_out_3), .out_2(merge_2_out_2),
    .out_1(merge_2_out_1));
  selector_3bits fecth_add (
    .bit2(merge_2_out_2), .bit1(merge_2_out_1), .bit0(merge_2_out_0), .CU_in(or_14_out),
    .bit2_out(fecth_add_bit2_out), .bit1_out(fecth_add_bit1_out), .bit0_out(fecth_add_bit0_out));
  or or_15 (or_15_out, merge_3_out_3, merge_2_out_3);
  or or_16 (or_16_out, CU6, CU6_2);
  merge merge_3 (
    .in_1_3(selector_4bit_1_bit3_out), .in_1_2(selector_4bit_1_bit2_out), .in_1_1(selector_4bit_1_bit1_out),
    .in_1_0(selector_4bit_1_bit0_out), .in_2_2(undriven_2), .in_2_1(undriven_3), .in_2_0(undriven_4),
    .out_0(merge_3_out_0), .out_3(merge_3_out_3), .out_2(merge_3_out_2), .out_1(merge_3_out_1));  // open: in_2_3
  merge merge_4 (
    .in_1_3(MBR_3), .in_1_2(MBR_2), .in_1_1(MBR_1), .in_1_0(MBR_0), .in_2_3(or_15_out),
    .in_2_2(merge_2_out_2), .in_2_1(merge_2_out_1), .in_2_0(merge_2_out_0), .out_0(merge_4_out_0),
    .out_3(merge_4_out_3), .out_2(merge_4_out_2), .out_1(merge_4_out_1));
  and and_9 (and_9_out, or_16_out, FETCH);
  selector_4bit selector_4bit_1 (
    .bit_3(or_35_out), .bit2(mar_1_mar_out_2), .bit1(mar_1_mar_out_1), .bit0(mar_1_mar_out_0),
    .CU_in(or_17_out), .bit2_out(selector_4bit_1_bit2_out), .bit1_out(selector_4bit_1_bit1_out),
    .bit0_out(selector_4bit_1_bit0_out), .bit3_out(selector_4bit_1_bit3_out));
  merge merge_5 (
    .in_1_3(merge_2_out_3), .in_1_2(merge_2_out_2), .in_1_1(merge_2_out_1), .in_1_0(merge_2_out_0),
    .in_2_3(or_35_out), .in_2_2(data_out_3_data_out_2), .in_2_1(data_out_3_data_out_1), .in_2_0(or_37_out),
    .out_0(merge_5_out_0), .out_3(merge_5_out_3), .out_2(merge_5_out_2), .out_1(merge_5_out_1));
  and and_10 (and_10_out, or_18_out, CU9_2);
  INCREAMENTER increamenter_1 (
    .INC_input_0(pc_1_pc_out_0), .INC_INPUT_1(pc_1_pc_out_1), .INC_input_2(pc_1_pc_out_2),
    .INC_out_0(increamenter_1_inc_out_0), .INC_out_1(increamenter_1_inc_out_1),
    .INC_out_2(increamenter_1_inc_out_2));
  or or_17 (or_17_out, and_9_out, CU1_2, CU1);
  MAR mar_1 (
    .MAR_2(merge_7_out_2), .MAR_1(merge_7_out_1), .MAR_0(merge_7_out_0), .CLOCK_MAR(or_21_out),
    .MAR_out_2(mar_1_mar_out_2), .MAr_out_1(mar_1_mar_out_1), .MAR_out_0(mar_1_mar_out_0));
  or or_18 (or_18_out, load_R0_1, arithmic, load_R0_0);
  or or_19 (or_19_out, CU7_2, CU8_2, CU3_2);
  merge merge_6 (
    .in_1_3(or_35_out), .in_1_2(data_out_3_data_out_2), .in_1_1(data_out_3_data_out_1), .in_1_0(or_37_out),
    .in_2_3(merge_4_out_3), .in_2_2(merge_4_out_2), .in_2_1(merge_4_out_1), .in_2_0(merge_4_out_0),
    .out_0(merge_6_out_0), .out_3(merge_6_out_3), .out_2(merge_6_out_2), .out_1(merge_6_out_1));
  Register_0 register_0_1 (
    .R0_input_3(merge_6_out_3), .R0_input_2(merge_6_out_2), .R0_input_1(merge_6_out_1),
    .R0_input_0(merge_6_out_0), .CLOCK_R_0(and_10_out), .R0_out_3(register_0_1_r0_out_3),
    .R0_out_1(register_0_1_r0_out_1), .R0_out_2(register_0_1_r0_out_2), .R0_out_0(register_0_1_r0_out_0));
  PC pc_1 (
    .PC_2(increamenter_1_inc_out_2), .PC_1(increamenter_1_inc_out_1), .PC_0(increamenter_1_inc_out_0),
    .CLOCK_PC(CU1_2), .PC_out_2(pc_1_pc_out_2), .PC_out_1(pc_1_pc_out_1), .PC_out_0(pc_1_pc_out_0));
  data_out data_out_1 (
    .clock(or_20_out), .CU(or_22_out), .data_in_3(register_0_1_r0_out_3), .data_in_2(register_0_1_r0_out_2),
    .data_in_1(register_0_1_r0_out_1), .data_in_0(register_0_1_r0_out_0), .merge3(or_15_out),
    .merge2(merge_2_out_2), .merge1(merge_2_out_1), .merge0(merge_2_out_0),
    .data_out_3(data_out_1_data_out_3), .data_out_2(data_out_1_data_out_2),
    .data_out_1(data_out_1_data_out_1), .data_out_0(data_out_1_data_out_0));
  or or_20 (or_20_out, CU7, and_12_out, and_13_out, CU7_2);
  or or_21 (or_21_out, CU5_2, CU0_2);
  merge merge_7 (
    .in_1_2(data_out_3_data_out_2), .in_1_1(data_out_3_data_out_1), .in_1_0(or_37_out),
    .in_2_2(selector_3bits_1_bit2_out), .in_2_1(selector_3bits_1_bit1_out),
    .in_2_0(selector_3bits_1_bit0_out), .out_0(merge_7_out_0), .out_2(merge_7_out_2), .out_1(merge_7_out_1));  // open: in_1_3, in_2_3, out_3
  MBR u_mbr_1 (
    .MBR_input_3(merge_5_out_3), .MBR_input_2(merge_5_out_2), .MBR_input_1(merge_5_out_1),
    .MBR_input_0(merge_5_out_0), .CLOCK_MBR(or_19_out), .MBR_out_3(mbr_1_mbr_out_3),
    .MBR_out_1(mbr_1_mbr_out_1), .MBR_out_2(mbr_1_mbr_out_2), .MBR_out_0(mbr_1_mbr_out_0));
  or or_22 (or_22_out, save_R0_1, ADD_R0, arithmic, SUB_R0, save_R1_0);
  or or_23 (or_23_out, CU0, CU0_2);
  or or_24 (or_24_out, CU8, CU9_2, CU9, CU8_2);
  or or_25 (or_25_out, load_R1_1, load_R1_0);
  selector_3bits selector_3bits_1 (
    .bit2(pc_1_pc_out_2), .bit1(pc_1_pc_out_1), .bit0(pc_1_pc_out_0), .CU_in(or_23_out),
    .bit2_out(selector_3bits_1_bit2_out), .bit1_out(selector_3bits_1_bit1_out),
    .bit0_out(selector_3bits_1_bit0_out));
  or or_26 (or_26_out, CU4, CU4_2);
  selector_4bit selector_4bit_2 (
    .bit_3(mbr_1_mbr_out_3), .bit2(mbr_1_mbr_out_2), .bit1(mbr_1_mbr_out_1), .bit0(mbr_1_mbr_out_0),
    .CU_in(or_24_out), .bit2_out(MBR_2), .bit1_out(MBR_1), .bit0_out(MBR_0), .bit3_out(MBR_3));
  and and_11 (and_11_out, CU9_2, or_25_out);
  or or_27 (or_27_out, ADD_R0, SUB_R0);
  and and_12 (and_12_out, or_27_out, or_28_out);
  and and_13 (and_13_out, arithmic, or_29_out);
  selector_4bit selector_4bit_3 (
    .bit_3(mbr_1_mbr_out_3), .bit2(mbr_1_mbr_out_2), .bit1(mbr_1_mbr_out_1), .bit0(mbr_1_mbr_out_0),
    .CU_in(or_26_out), .bit2_out(selector_4bit_3_bit2_out), .bit1_out(selector_4bit_3_bit1_out),
    .bit0_out(selector_4bit_3_bit0_out), .bit3_out(selector_4bit_3_bit3_out));
  or or_28 (or_28_out, CU5, CU5_2);
  merge merge_8 (
    .in_1_3(or_35_out), .in_1_2(data_out_3_data_out_2), .in_1_1(data_out_3_data_out_1), .in_1_0(or_37_out),
    .in_2_3(merge_4_out_3), .in_2_2(merge_4_out_2), .in_2_1(merge_4_out_1), .in_2_0(merge_4_out_0),
    .out_0(merge_8_out_0), .out_3(merge_8_out_3), .out_2(merge_8_out_2), .out_1(merge_8_out_1));
  Register_1 register_1_1 (
    .R1_input_3(merge_8_out_3), .R1_input_2(merge_8_out_2), .R1_input_1(merge_8_out_1),
    .R1_input_0(merge_8_out_0), .CLOCK_R_1(and_11_out), .R1_out_3(register_1_1_r1_out_3),
    .R1_out_1(register_1_1_r1_out_1), .R1_out_2(register_1_1_r1_out_2), .R1_out_0(register_1_1_r1_out_0));
  data_out data_out_2 (
    .clock(or_30_out), .CU(or_31_out), .data_in_3(register_1_1_r1_out_3), .data_in_2(register_1_1_r1_out_2),
    .data_in_1(register_1_1_r1_out_1), .data_in_0(register_1_1_r1_out_0), .merge3(data_out_1_data_out_3),
    .merge2(data_out_1_data_out_2), .merge1(data_out_1_data_out_1), .merge0(data_out_1_data_out_0),
    .data_out_3(data_out_2_data_out_3), .data_out_2(data_out_2_data_out_2),
    .data_out_1(data_out_2_data_out_1), .data_out_0(data_out_2_data_out_0));
  or or_29 (or_29_out, CU6, CU6_2);
  or or_30 (or_30_out, CU7, and_14_out, CU7_2);
  IR ir_1 (
    .IR_input_3(selector_4bit_3_bit3_out), .IR_input_2(selector_4bit_3_bit2_out),
    .IR_input_1(selector_4bit_3_bit1_out), .IR_input_0(selector_4bit_3_bit0_out), .CLOCK_IR(CU4_2),
    .IR_out_3(ir_1_ir_out_3), .IR_out_2(ir_1_ir_out_2), .IR_out_1(ir_1_ir_out_1), .IR_out_0(ir_1_ir_out_0));
  CU cu_1 (
    .IN0(ir_1_ir_out_0), .IN2(ir_1_ir_out_2), .IN3(ir_1_ir_out_3), .IN1(ir_1_ir_out_1),
    .LOAD_R1_0(load_R1_1), .LOAD_R1_1(load_R1_0), .LOAD_R0_1(load_R0_1), .LOAD_R0_0(load_R0_0),
    .SAVE_R1_0(save_R1_0), .SAVE_R1_1(save_R1_1), .SAVE_R0_1(save_R0_1), .SAVE_R0_0(save_R0_0),
    .ADD_R1_out(ADD_R1), .ADD_R0_out(ADD_R0), .SUB_R1_out(SUB_R1), .SUB_R0_out(SUB_R0), .HALT(HALT));
  or or_31 (or_31_out, save_R1_1, ADD_R1, SUB_R1, save_R1_0);
  or or_32 (load, load_R0_1, load_R1_1, load_R1_0, load_R0_0);
  or or_33 (or_33_out, ADD_R1, SUB_R1);
  and and_14 (and_14_out, or_33_out, or_34_out);
  or or_34 (or_34_out, CU5, CU5_2);
  or or_35 (or_35_out, data_out_3_data_out_3, and_15_out);
  or or_36 (write, save_R0_1, save_R1_1, save_R1_0, save_R0_0);
  and and_15 (and_15_out, write, or_38_out);
  or or_37 (or_37_out, address_1_out, data_out_3_data_out_0);
  or or_38 (or_38_out, CU6, CU6_2);
  and and_16 (and_16_out, arithmic, CU6_2);
  or or_39 (or_39_out, SUB_R1, SUB_R0);
  Clock clock_1 (.out(clock_1_out));
  not not_1 (not_1_out, HALT);
  or or_40 (or_40_out, load_R1_1, load_R0_1, save_R1_1, save_R0_1);
  and address_1 (address_1_out, or_40_out, or_41_out);
  and and_17 (and_17_out, clock_1_out, not_1_out);
  modulo control_unit_2 (
    .clock(and_17_out), .out0(CU0), .out1(CU0_2), .out2(CU1), .out3(CU1_2), .out4(CU2), .out5(CU2_2),
    .out6(CU3), .out7(CU3_2), .out8(CU4), .out9(CU4_2), .out10(CU5), .out11(CU5_2), .out12(CU6),
    .out13(CU6_2), .out14(CU7), .out15(CU7_2), .out16(CU8), .out17(CU8_2), .out18(CU9), .out19(CU9_2));
  or or_41 (or_41_out, CU5, CU5_2);
  Register_0 LEFT (
    .R0_input_3(data_out_3_data_out_3), .R0_input_2(data_out_3_data_out_2),
    .R0_input_1(data_out_3_data_out_1), .R0_input_0(data_out_3_data_out_0), .CLOCK_R_0(and_16_out),
    .R0_out_3(LEFT_r0_out_3), .R0_out_1(LEFT_r0_out_1), .R0_out_2(LEFT_r0_out_2), .R0_out_0(LEFT_r0_out_0));
  and and_18 (and_18_out, arithmic, CU7);
  and and_19 (and_19_out, arithmic, CU5_2);
  ALU_a6 alu_a6_1 (
    .R3(Right_r0_out_3), .R2(Right_r0_out_2), .R1(Right_r0_out_1), .R0(Right_r0_out_0), .L3(LEFT_r0_out_3),
    .L2(LEFT_r0_out_2), .L1(LEFT_r0_out_1), .L0(LEFT_r0_out_0), .ADD_SUB(or_39_out),
    .overflow(alu_a6_1_overflow), .zero(alu_a6_1_zero), .negative(alu_a6_1_negative), .out3(alu_a6_1_out3),
    .out2(alu_a6_1_out2), .out1(alu_a6_1_out1), .out0(alu_a6_1_out0));  // open: clock
  or or_42 (arithmic, ADD_R1, ADD_R0, SUB_R1, SUB_R0);
  Register_0 Right (
    .R0_input_3(data_out_3_data_out_3), .R0_input_2(data_out_3_data_out_2),
    .R0_input_1(data_out_3_data_out_1), .R0_input_0(data_out_3_data_out_0), .CLOCK_R_0(and_19_out),
    .R0_out_3(Right_r0_out_3), .R0_out_1(Right_r0_out_1), .R0_out_2(Right_r0_out_2), .R0_out_0(Right_r0_out_0));
  Display display_1 (
    .in_1(RAM_0_3), .in_2(RAM_0_2), .in_3(RAM_0_1), .in_4(RAM_0_0), .reg_1(display_1_reg_1),
    .reg_2(display_1_reg_2), .reg_3(display_1_reg_3), .reg_4(display_1_reg_4), .reg_5(display_1_reg_5),
    .reg_6(display_1_reg_6), .reg_7(display_1_reg_7), .out_12(display_1_out_12));
  Register_0 register_0_2 (
    .R0_input_3(alu_a6_1_out3), .R0_input_2(alu_a6_1_out2), .R0_input_1(alu_a6_1_out1),
    .R0_input_0(alu_a6_1_out0), .CLOCK_R_0(and_18_out), .R0_out_3(register_0_2_r0_out_3),
    .R0_out_1(register_0_2_r0_out_1), .R0_out_2(register_0_2_r0_out_2), .R0_out_0(register_0_2_r0_out_0));
  not not_2 (not_2_out, display_1_out_12);
  and and_20 (and_20_out, arithmic, CU7_2);
  data_out data_out_3 (
    .clock(or_44_out), .CU(arithmic), .data_in_3(register_0_2_r0_out_3), .data_in_2(register_0_2_r0_out_2),
    .data_in_1(register_0_2_r0_out_1), .data_in_0(register_0_2_r0_out_0), .merge3(data_out_2_data_out_3),
    .merge2(data_out_2_data_out_2), .merge1(data_out_2_data_out_1), .merge0(data_out_2_data_out_0),
    .data_out_3(data_out_3_data_out_3), .data_out_2(data_out_3_data_out_2),
    .data_out_1(data_out_3_data_out_1), .data_out_0(data_out_3_data_out_0));
  or or_43 (FETCH, load, write);
  STATUS status_1 (
    .overflow(alu_a6_1_overflow), .negtive(alu_a6_1_negative), .zero(alu_a6_1_zero), .clock(and_20_out));  // open: negtive_out, overflow_out, zero_out
  or or_44 (or_44_out, CU9, CU9_2);
  _7_Segment_Display u_7_segment_display_1 (
    .f(not_2_out), .a(not_2_out), .b(or_45_out), .e(not_2_out), .d(not_2_out), .c(or_46_out));  // open: g, dp
  or or_45 (or_45_out, not_2_out, display_1_out_12);
  or or_46 (or_46_out, not_2_out, display_1_out_12);
  _7_Segment_Display u_7_segment_display_2 (
    .g(display_1_reg_4), .f(display_1_reg_2), .a(display_1_reg_1), .b(display_1_reg_3), .e(display_1_reg_5),
    .d(display_1_reg_7), .c(display_1_reg_6));  // open: dp

  // Notes on the sheet:
  //   cu1
endmodule

module RAM_A5 (
  input  CLOCK_RAM,
  input  add2,
  input  add1,
  input  add0,
  input  mode,
  input  data3,
  input  data2,
  input  data1,
  input  data0,
  output output3,
  output output2,
  output output1,
  output output0,
  output RAM_0_3,
  output RAM_0_2,
  output RAM_0_1,
  output RAM_0_0
);

  wire and_1_out, and_2_out, and_3_out, and_4_out, and_5_out, and_6_out, and_7_out, and_8_out, and_9_out,
       and_10_out, and_11_out, and_12_out, and_13_out, and_14_out, and_15_out, and_16_out, and_17_out,
       and_18_out, and_19_out, and_20_out, and_21_out, and_22_out, and_23_out, and_24_out, and_25_out,
       and_26_out, and_27_out, and_28_out, and_29_out, and_30_out, and_31_out, and_32_out, and_33_out,
       and_34_out, and_35_out, and_36_out, and_37_out, and_38_out, and_39_out, and_40_out, and_41_out,
       and_42_out, and_43_out, and_44_out, and_45_out, and_46_out, and_47_out, and_48_out, and_49_out,
       and_50_out, and_51_out, and_52_out, and_53_out, and_54_out, and_55_out, and_56_out, and_57_out,
       and_58_out, and_59_out, and_60_out, and_61_out, and_62_out, and_63_out, and_64_out, and_65_out,
       and_66_out, and_67_out, and_68_out, and_69_out, and_70_out, and_71_out, and_72_out, and_73_out,
       and_74_out, and_75_out, and_76_out, and_77_out, and_78_out, and_79_out, and_80_out, d_ff_1_q,
       d_ff_2_q, d_ff_3_q, d_ff_4_q, d_ff_5_q, d_ff_6_q, d_ff_7_q, d_ff_9_q, d_ff_10_q, d_ff_11_q, d_ff_12_q,
       d_ff_13_q, d_ff_14_q, d_ff_15_q, d_ff_21_q, d_ff_22_q, d_ff_23_q, d_ff_24_q, d_ff_25_q, d_ff_26_q,
       d_ff_27_q, d_ff_29_q, d_ff_30_q, d_ff_31_q, d_ff_32_q, d_ff_33_q, d_ff_34_q, d_ff_35_q, not_1_out,
       not_2_out, not_3_out, not_4_out, not_5_out, not_6_out, not_7_out, not_8_out, not_9_out, not_10_out,
       not_11_out, not_12_out, not_13_out, or_1_out, or_2_out, or_3_out, or_4_out;

  not not_1 (not_1_out, add0);
  not not_2 (not_2_out, add1);
  not not_3 (not_3_out, add1);
  not not_4 (not_4_out, add0);
  not not_5 (not_5_out, add2);
  not not_6 (not_6_out, add2);
  not not_7 (not_7_out, add0);
  not not_8 (not_8_out, add2);
  not not_9 (not_9_out, add1);
  not not_10 (not_10_out, add2);
  not not_11 (not_11_out, add1);
  not not_12 (not_12_out, add0);
  and and_1 (and_1_out, add2, add1, CLOCK_RAM, add0);
  and and_2 (and_2_out, and_1_out, mode);
  and and_3 (and_3_out, add2, add1, CLOCK_RAM, not_1_out);
  and and_4 (and_4_out, and_3_out, mode);
  and and_5 (and_5_out, add2, not_2_out, CLOCK_RAM, add0);
  and and_6 (and_6_out, and_5_out, mode);
  and and_7 (and_7_out, add2, not_3_out, CLOCK_RAM, not_4_out);
  and and_8 (and_8_out, and_7_out, mode);
  and and_9 (and_9_out, not_5_out, add1, CLOCK_RAM, add0);
  and and_10 (and_10_out, and_9_out, mode);
  and and_11 (and_11_out, not_6_out, add1, CLOCK_RAM, not_7_out);
  and and_12 (and_12_out, and_11_out, mode);
  and and_13 (and_13_out, not_8_out, not_9_out, CLOCK_RAM, add0);
  and and_14 (and_14_out, and_13_out, mode);
  and and_15 (and_15_out, not_10_out, not_11_out, CLOCK_RAM, not_12_out);
  and and_16 (and_16_out, and_15_out, mode);
  and and_17 (and_17_out, and_1_out, mode, data3);
  D_Flip_Flop #(.trigger("high")) d_ff_1 (.D(and_17_out), .clk(and_2_out), .Q(d_ff_1_q));  // open: Qn, preset, reset
  and and_18 (and_18_out, and_3_out, mode, data3);
  D_Flip_Flop #(.trigger("high")) d_ff_2 (.D(and_18_out), .clk(and_4_out), .Q(d_ff_2_q));  // open: Qn, preset, reset
  and and_19 (and_19_out, and_5_out, mode, data3);
  D_Flip_Flop #(.trigger("high")) d_ff_3 (.D(and_19_out), .clk(and_6_out), .Q(d_ff_3_q));  // open: Qn, preset, reset
  and and_20 (and_20_out, and_7_out, mode, data3);
  D_Flip_Flop #(.trigger("high")) d_ff_4 (.D(and_20_out), .clk(and_8_out), .Q(d_ff_4_q));  // open: Qn, preset, reset
  and and_21 (and_21_out, and_9_out, mode, data3);
  D_Flip_Flop #(.trigger("high")) d_ff_5 (.D(and_21_out), .clk(and_10_out), .Q(d_ff_5_q));  // open: Qn, preset, reset
  and and_22 (and_22_out, and_11_out, mode, data3);
  D_Flip_Flop #(.trigger("high")) d_ff_6 (.D(and_22_out), .clk(and_12_out), .Q(d_ff_6_q));  // open: Qn, preset, reset
  and and_23 (and_23_out, and_13_out, mode, data3);
  D_Flip_Flop #(.trigger("high")) d_ff_7 (.D(and_23_out), .clk(and_14_out), .Q(d_ff_7_q));  // open: Qn, preset, reset
  and and_24 (and_24_out, and_15_out, mode, data3);
  D_Flip_Flop #(.trigger("high")) d_ff_8 (.D(and_24_out), .clk(and_16_out), .Q(RAM_0_3));  // open: Qn, preset, reset
  not not_13 (not_13_out, mode);
  Clock clock_1 ();  // open: out
  or or_1 (or_1_out, and_25_out, and_26_out, and_27_out, and_28_out, and_29_out, and_30_out, and_31_out, and_32_out);
  and and_25 (and_25_out, d_ff_1_q, and_1_out, not_13_out);
  and and_26 (and_26_out, d_ff_2_q, and_3_out, not_13_out);
  and and_27 (and_27_out, d_ff_3_q, and_5_out, not_13_out);
  and and_28 (and_28_out, d_ff_4_q, and_7_out, not_13_out);
  and and_29 (and_29_out, d_ff_5_q, and_9_out, not_13_out);
  and and_30 (and_30_out, d_ff_6_q, and_11_out, not_13_out);
  and and_31 (and_31_out, d_ff_7_q, and_13_out, not_13_out);
  and and_32 (and_32_out, RAM_0_3, and_15_out, not_13_out);
  and and_33 (and_33_out, and_1_out, mode, data2);
  D_Flip_Flop #(.trigger("high")) d_ff_9 (.D(and_33_out), .clk(and_2_out), .Q(d_ff_9_q));  // open: Qn, preset, reset
  and and_34 (and_34_out, and_3_out, mode, data2);
  D_Flip_Flop #(.trigger("high")) d_ff_10 (.D(and_34_out), .clk(and_4_out), .Q(d_ff_10_q));  // open: Qn, preset, reset
  and and_35 (and_35_out, and_5_out, mode, data2);
  D_Flip_Flop #(.trigger("high")) d_ff_11 (.D(and_35_out), .clk(and_6_out), .Q(d_ff_11_q));  // open: Qn, preset, reset
  and and_36 (and_36_out, and_7_out, mode, data2);
  D_Flip_Flop #(.trigger("high")) d_ff_12 (.D(and_36_out), .clk(and_8_out), .Q(d_ff_12_q));  // open: Qn, preset, reset
  and and_37 (and_37_out, and_9_out, mode, data2);
  D_Flip_Flop #(.trigger("high")) d_ff_13 (.D(and_37_out), .clk(and_10_out), .Q(d_ff_13_q));  // open: Qn, preset, reset
  and and_38 (and_38_out, and_11_out, mode, data2);
  D_Flip_Flop #(.trigger("high")) d_ff_14 (.D(and_38_out), .clk(and_12_out), .Q(d_ff_14_q));  // open: Qn, preset, reset
  and and_39 (and_39_out, and_13_out, mode, data2);
  D_Flip_Flop #(.trigger("high")) d_ff_15 (.D(and_39_out), .clk(and_14_out), .Q(d_ff_15_q));  // open: Qn, preset, reset
  and and_40 (and_40_out, and_15_out, mode, data2);
  D_Flip_Flop #(.trigger("high")) d_ff_16 (.D(and_40_out), .clk(and_16_out), .Q(RAM_0_2));  // open: Qn, preset, reset
  D_Flip_Flop #(.trigger("high")) d_ff_17 (.D(or_1_out), .clk(CLOCK_RAM), .Q(output3));  // open: Qn, preset, reset
  or or_2 (or_2_out, and_41_out, and_42_out, and_43_out, and_44_out, and_45_out, and_46_out, and_47_out, and_48_out);
  and and_41 (and_41_out, d_ff_9_q, and_1_out, not_13_out);
  and and_42 (and_42_out, d_ff_10_q, and_3_out, not_13_out);
  and and_43 (and_43_out, d_ff_11_q, and_5_out, not_13_out);
  and and_44 (and_44_out, d_ff_12_q, and_7_out, not_13_out);
  and and_45 (and_45_out, d_ff_13_q, and_9_out, not_13_out);
  and and_46 (and_46_out, d_ff_14_q, and_11_out, not_13_out);
  and and_47 (and_47_out, d_ff_15_q, and_13_out, not_13_out);
  and and_48 (and_48_out, RAM_0_2, and_15_out, not_13_out);
  D_Flip_Flop #(.trigger("high")) d_ff_18 (.D(or_2_out), .clk(CLOCK_RAM), .Q(output2));  // open: Qn, preset, reset
  D_Flip_Flop #(.trigger("high")) d_ff_19 (.D(or_3_out), .clk(CLOCK_RAM), .Q(output1));  // open: Qn, preset, reset
  D_Flip_Flop #(.trigger("high")) d_ff_20 (.D(or_4_out), .clk(CLOCK_RAM), .Q(output0));  // open: Qn, preset, reset
  and and_49 (and_49_out, and_1_out, mode, data1);
  D_Flip_Flop #(.trigger("high")) d_ff_21 (.D(and_49_out), .clk(and_2_out), .Q(d_ff_21_q));  // open: Qn, preset, reset
  and and_50 (and_50_out, and_3_out, mode, data1);
  D_Flip_Flop #(.trigger("high")) d_ff_22 (.D(and_50_out), .clk(and_4_out), .Q(d_ff_22_q));  // open: Qn, preset, reset
  and and_51 (and_51_out, and_5_out, mode, data1);
  D_Flip_Flop #(.trigger("high")) d_ff_23 (.D(and_51_out), .clk(and_6_out), .Q(d_ff_23_q));  // open: Qn, preset, reset
  and and_52 (and_52_out, and_7_out, mode, data1);
  D_Flip_Flop #(.trigger("high")) d_ff_24 (.D(and_52_out), .clk(and_8_out), .Q(d_ff_24_q));  // open: Qn, preset, reset
  and and_53 (and_53_out, and_9_out, mode, data1);
  D_Flip_Flop #(.trigger("high")) d_ff_25 (.D(and_53_out), .clk(and_10_out), .Q(d_ff_25_q));  // open: Qn, preset, reset
  and and_54 (and_54_out, and_11_out, mode, data1);
  D_Flip_Flop #(.trigger("high")) d_ff_26 (.D(and_54_out), .clk(and_12_out), .Q(d_ff_26_q));  // open: Qn, preset, reset
  and and_55 (and_55_out, and_13_out, mode, data1);
  D_Flip_Flop #(.trigger("high")) d_ff_27 (.D(and_55_out), .clk(and_14_out), .Q(d_ff_27_q));  // open: Qn, preset, reset
  and and_56 (and_56_out, and_15_out, mode, data1);
  D_Flip_Flop #(.trigger("high")) d_ff_28 (.D(and_56_out), .clk(and_16_out), .Q(RAM_0_1));  // open: Qn, preset, reset
  or or_3 (or_3_out, and_57_out, and_58_out, and_59_out, and_60_out, and_61_out, and_62_out, and_63_out, and_64_out);
  and and_57 (and_57_out, d_ff_21_q, and_1_out, not_13_out);
  and and_58 (and_58_out, d_ff_22_q, and_3_out, not_13_out);
  and and_59 (and_59_out, d_ff_23_q, and_5_out, not_13_out);
  and and_60 (and_60_out, d_ff_24_q, and_7_out, not_13_out);
  and and_61 (and_61_out, d_ff_25_q, and_9_out, not_13_out);
  and and_62 (and_62_out, d_ff_26_q, and_11_out, not_13_out);
  and and_63 (and_63_out, d_ff_27_q, and_13_out, not_13_out);
  and and_64 (and_64_out, RAM_0_1, and_15_out, not_13_out);
  and and_65 (and_65_out, and_1_out, mode, data0);
  D_Flip_Flop #(.trigger("high")) d_ff_29 (.D(and_65_out), .clk(and_2_out), .Q(d_ff_29_q));  // open: Qn, preset, reset
  and and_66 (and_66_out, and_3_out, mode, data0);
  D_Flip_Flop #(.trigger("high")) d_ff_30 (.D(and_66_out), .clk(and_4_out), .Q(d_ff_30_q));  // open: Qn, preset, reset
  and and_67 (and_67_out, and_5_out, mode, data0);
  D_Flip_Flop #(.trigger("high")) d_ff_31 (.D(and_67_out), .clk(and_6_out), .Q(d_ff_31_q));  // open: Qn, preset, reset
  and and_68 (and_68_out, and_7_out, mode, data0);
  D_Flip_Flop #(.trigger("high")) d_ff_32 (.D(and_68_out), .clk(and_8_out), .Q(d_ff_32_q));  // open: Qn, preset, reset
  and and_69 (and_69_out, and_9_out, mode, data0);
  D_Flip_Flop #(.trigger("high")) d_ff_33 (.D(and_69_out), .clk(and_10_out), .Q(d_ff_33_q));  // open: Qn, preset, reset
  and and_70 (and_70_out, and_11_out, mode, data0);
  D_Flip_Flop #(.trigger("high")) d_ff_34 (.D(and_70_out), .clk(and_12_out), .Q(d_ff_34_q));  // open: Qn, preset, reset
  and and_71 (and_71_out, and_13_out, mode, data0);
  D_Flip_Flop #(.trigger("high")) d_ff_35 (.D(and_71_out), .clk(and_14_out), .Q(d_ff_35_q));  // open: Qn, preset, reset
  and and_72 (and_72_out, and_15_out, mode, data0);
  D_Flip_Flop #(.trigger("high")) d_ff_36 (.D(and_72_out), .clk(and_16_out), .Q(RAM_0_0));  // open: Qn, preset, reset
  or or_4 (or_4_out, and_73_out, and_74_out, and_75_out, and_76_out, and_77_out, and_78_out, and_79_out, and_80_out);
  and and_73 (and_73_out, d_ff_29_q, and_1_out, not_13_out);
  and and_74 (and_74_out, d_ff_30_q, and_3_out, not_13_out);
  and and_75 (and_75_out, d_ff_31_q, and_5_out, not_13_out);
  and and_76 (and_76_out, d_ff_32_q, and_7_out, not_13_out);
  and and_77 (and_77_out, d_ff_33_q, and_9_out, not_13_out);
  and and_78 (and_78_out, d_ff_34_q, and_11_out, not_13_out);
  and and_79 (and_79_out, d_ff_35_q, and_13_out, not_13_out);
  and and_80 (and_80_out, RAM_0_0, and_15_out, not_13_out);

  // Notes on the sheet:
  //   3-bit address input pins
  //   Mode input pin
  //   4-bit data input pins
  //   4-bit data output pins
endmodule

module PC (
  input  PC_2,
  input  PC_1,
  input  PC_0,
  input  CLOCK_PC,
  output PC_out_2,
  output PC_out_1,
  output PC_out_0
);

  D_Flip_Flop d_ff_1 (.D(PC_2), .clk(CLOCK_PC), .Q(PC_out_2));  // open: Qn, preset, reset
  D_Flip_Flop d_ff_2 (.D(PC_1), .clk(CLOCK_PC), .Q(PC_out_1));  // open: Qn, preset, reset
  D_Flip_Flop d_ff_3 (.D(PC_0), .clk(CLOCK_PC), .Q(PC_out_0));  // open: Qn, preset, reset
endmodule

module INCREAMENTER (
  input  INC_input_0,
  input  INC_INPUT_1,
  input  INC_input_2,
  output INC_out_0,
  output INC_out_1,
  output INC_out_2
);

  wire and_1_out, and_2_out;

  xor xor_1 (INC_out_0, 1'b1, INC_input_0);
  and and_1 (and_1_out, 1'b1, INC_input_0);
  xor xor_2 (INC_out_1, and_1_out, INC_INPUT_1);
  and and_2 (and_2_out, and_1_out, INC_INPUT_1);
  xor xor_3 (INC_out_2, and_2_out, INC_input_2);
  // AND_Gate and_3 has open pins: in0=and_2_out, in1=INC_input_2, out=open
endmodule

module Register_0 (
  input  R0_input_3,
  input  R0_input_2,
  input  R0_input_1,
  input  R0_input_0,
  input  CLOCK_R_0,
  output R0_out_3,
  output R0_out_1,
  output R0_out_2,
  output R0_out_0
);

  D_Flip_Flop d_ff_1 (.D(R0_input_3), .clk(CLOCK_R_0), .Q(R0_out_3));  // open: Qn, preset, reset
  D_Flip_Flop d_ff_2 (.D(R0_input_2), .clk(CLOCK_R_0), .Q(R0_out_2));  // open: Qn, preset, reset
  D_Flip_Flop d_ff_3 (.D(R0_input_1), .clk(CLOCK_R_0), .Q(R0_out_1));  // open: Qn, preset, reset
  D_Flip_Flop d_ff_4 (.D(R0_input_0), .clk(CLOCK_R_0), .Q(R0_out_0));  // open: Qn, preset, reset
endmodule

module Register_1 (
  input  R1_input_3,
  input  R1_input_2,
  input  R1_input_1,
  input  R1_input_0,
  input  CLOCK_R_1,
  output R1_out_3,
  output R1_out_1,
  output R1_out_2,
  output R1_out_0
);

  D_Flip_Flop d_ff_1 (.D(R1_input_3), .clk(CLOCK_R_1), .Q(R1_out_3));  // open: Qn, preset, reset
  D_Flip_Flop d_ff_2 (.D(R1_input_2), .clk(CLOCK_R_1), .Q(R1_out_2));  // open: Qn, preset, reset
  D_Flip_Flop d_ff_3 (.D(R1_input_1), .clk(CLOCK_R_1), .Q(R1_out_1));  // open: Qn, preset, reset
  D_Flip_Flop d_ff_4 (.D(R1_input_0), .clk(CLOCK_R_1), .Q(R1_out_0));  // open: Qn, preset, reset
endmodule

module IR (
  input  IR_input_3,
  input  IR_input_2,
  input  IR_input_1,
  input  IR_input_0,
  input  CLOCK_IR,
  output IR_out_3,
  output IR_out_2,
  output IR_out_1,
  output IR_out_0
);

  D_Flip_Flop d_ff_1 (.D(IR_input_3), .clk(CLOCK_IR), .Q(IR_out_3));  // open: Qn, preset, reset
  D_Flip_Flop d_ff_2 (.D(IR_input_2), .clk(CLOCK_IR), .Q(IR_out_2));  // open: Qn, preset, reset
  D_Flip_Flop d_ff_3 (.D(IR_input_1), .clk(CLOCK_IR), .Q(IR_out_1));  // open: Qn, preset, reset
  D_Flip_Flop d_ff_4 (.D(IR_input_0), .clk(CLOCK_IR), .Q(IR_out_0));  // open: Qn, preset, reset
endmodule

module MAR (
  input  MAR_2,
  input  MAR_1,
  input  MAR_0,
  input  CLOCK_MAR,
  output MAR_out_2,
  output MAr_out_1,
  output MAR_out_0
);

  D_Flip_Flop d_ff_1 (.D(MAR_2), .clk(CLOCK_MAR), .Q(MAR_out_2));  // open: Qn, preset, reset
  D_Flip_Flop d_ff_2 (.D(MAR_1), .clk(CLOCK_MAR), .Q(MAr_out_1));  // open: Qn, preset, reset
  D_Flip_Flop d_ff_3 (.D(MAR_0), .clk(CLOCK_MAR), .Q(MAR_out_0));  // open: Qn, preset, reset
endmodule

module MBR (
  input  MBR_input_3,
  input  MBR_input_2,
  input  MBR_input_1,
  input  MBR_input_0,
  input  CLOCK_MBR,
  output MBR_out_3,
  output MBR_out_1,
  output MBR_out_2,
  output MBR_out_0
);

  D_Flip_Flop d_ff_1 (.D(MBR_input_3), .clk(CLOCK_MBR), .Q(MBR_out_3));  // open: Qn, preset, reset
  D_Flip_Flop d_ff_2 (.D(MBR_input_2), .clk(CLOCK_MBR), .Q(MBR_out_2));  // open: Qn, preset, reset
  D_Flip_Flop d_ff_3 (.D(MBR_input_1), .clk(CLOCK_MBR), .Q(MBR_out_1));  // open: Qn, preset, reset
  D_Flip_Flop d_ff_4 (.D(MBR_input_0), .clk(CLOCK_MBR), .Q(MBR_out_0));  // open: Qn, preset, reset
endmodule

module DR (
  input  DR_IN_3,
  input  DR_IN_2,
  input  DR_IN_1,
  input  DR_IN_0,
  input  CLOCK_DR,
  output DR_3,
  output DR_2,
  output DR_1,
  output DR_0
);

  D_Flip_Flop d_ff_1 (.D(DR_IN_3), .clk(CLOCK_DR), .Q(DR_3));  // open: Qn, preset, reset
  D_Flip_Flop d_ff_2 (.D(DR_IN_2), .clk(CLOCK_DR), .Q(DR_2));  // open: Qn, preset, reset
  D_Flip_Flop d_ff_3 (.D(DR_IN_1), .clk(CLOCK_DR), .Q(DR_1));  // open: Qn, preset, reset
  D_Flip_Flop d_ff_4 (.D(DR_IN_0), .clk(CLOCK_DR), .Q(DR_0));  // open: Qn, preset, reset
endmodule

module AR (
  input  AR_IN_2,
  input  AR_IN_1,
  input  AR_IN_0,
  input  CLOCK_AR,
  output AR_out_2,
  output AR_out_1,
  output AR_out_0
);

  D_Flip_Flop d_ff_1 (.D(AR_IN_2), .clk(CLOCK_AR), .Q(AR_out_2));  // open: Qn, preset, reset
  D_Flip_Flop d_ff_2 (.D(AR_IN_1), .clk(CLOCK_AR), .Q(AR_out_1));  // open: Qn, preset, reset
  D_Flip_Flop d_ff_3 (.D(AR_IN_0), .clk(CLOCK_AR), .Q(AR_out_0));  // open: Qn, preset, reset
endmodule

module MODE (
  input  MODE_IN,
  input  CLOCK_MODE,
  output MODE_OUT
);

  D_Flip_Flop d_ff_1 (.D(MODE_IN), .clk(CLOCK_MODE), .Q(MODE_OUT));  // open: Qn, preset, reset
endmodule

module CU (
  input  IN0,
  input  IN2,
  input  IN3,
  input  IN1,
  output LOAD_R1_0,
  output LOAD_R1_1,
  output LOAD_R0_1,
  output LOAD_R0_0,
  output SAVE_R1_0,
  output SAVE_R1_1,
  output SAVE_R0_1,
  output SAVE_R0_0,
  output ADD_R1_out,
  output ADD_R0_out,
  output SUB_R1_out,
  output SUB_R0_out,
  output HALT
);

  wire A_out, L_0_out, L_1_out, L_out, not_1_out, not_2_out, not_3_out, not_4_out, not_5_out, not_6_out,
       not_7_out, not_8_out, not_9_out, not_10_out, not_11_out, not_12_out, not_13_out, not_14_out, S_0_out,
       S_1_out, S_out, SU_out;

  // AND_Gate and_1 is placed but not wired
  not not_1 (not_1_out, IN3);
  not not_2 (not_2_out, IN2);
  not not_3 (not_3_out, IN3);
  not not_4 (not_4_out, IN0);
  not not_5 (not_5_out, IN2);
  not not_6 (not_6_out, IN0);
  and L (L_out, not_1_out, not_2_out);
  and S (S_out, not_3_out, IN2);
  and A (A_out, IN3, not_4_out, not_5_out);
  and SU (SU_out, IN3, not_6_out, IN2);
  and H (HALT, IN0, IN1, IN2, IN3);
  not not_7 (not_7_out, IN1);
  not not_8 (not_8_out, IN1);
  and L_1 (L_1_out, L_out, IN1);
  and L_0 (L_0_out, not_7_out, L_out);
  and S_1 (S_1_out, S_out, IN1);
  and S_0 (S_0_out, not_8_out, S_out);
  not not_9 (not_9_out, IN1);
  not not_10 (not_10_out, IN1);
  not not_11 (not_11_out, IN0);
  and A_R0 (ADD_R0_out, A_out, not_9_out);
  and and_2 (SUB_R0_out, SU_out, not_10_out);
  not not_12 (not_12_out, IN0);
  not not_13 (not_13_out, IN0);
  not not_14 (not_14_out, IN0);
  and A_R1 (ADD_R1_out, IN1, A_out);
  and and_3 (SUB_R1_out, IN1, SU_out);
  and L_1_0 (LOAD_R1_0, L_1_out, not_11_out);
  and L_1_1 (LOAD_R1_1, L_1_out, IN0);
  and L_0_1 (LOAD_R0_1, L_0_out, IN0);
  and L_0_0 (LOAD_R0_0, L_0_out, not_12_out);
  and S_1_0 (SAVE_R1_0, S_1_out, not_13_out);
  and S_1_1 (SAVE_R1_1, S_1_out, IN0);
  and S_0_1 (SAVE_R0_1, S_0_out, IN0);
  and S_0_0 (SAVE_R0_0, S_0_out, not_14_out);
endmodule

module selector_3bits (
  input  bit2,
  input  bit1,
  input  bit0,
  input  CU_in,
  output bit2_out,
  output bit1_out,
  output bit0_out
);

  and and_1 (bit2_out, bit2, CU_in);
  and and_2 (bit1_out, bit1, CU_in);
  and and_3 (bit0_out, bit0, CU_in);
endmodule

module selector_4bit (
  input  bit_3,
  input  bit2,
  input  bit1,
  input  bit0,
  input  CU_in,
  output bit2_out,
  output bit1_out,
  output bit0_out,
  output bit3_out
);

  and and_1 (bit3_out, bit_3, CU_in);
  and and_2 (bit2_out, bit2, CU_in);
  and and_3 (bit1_out, bit1, CU_in);
  and and_4 (bit0_out, bit0, CU_in);
endmodule

module merge (
  input  in_1_3,
  input  in_1_2,
  input  in_1_1,
  input  in_1_0,
  input  in_2_3,
  input  in_2_2,
  input  in_2_1,
  input  in_2_0,
  output out_0,
  output out_3,
  output out_2,
  output out_1
);

  or or_1 (out_3, in_1_3, in_2_3);
  or or_2 (out_2, in_1_2, in_2_2);
  or or_3 (out_1, in_1_1, in_2_1);
  or or_4 (out_0, in_1_0, in_2_0);
endmodule

module data_out (
  input  clock,
  input  CU,
  input  data_in_3,
  input  data_in_2,
  input  data_in_1,
  input  data_in_0,
  input  merge3,
  input  merge2,
  input  merge1,
  input  merge0,
  output data_out_3,
  output data_out_2,
  output data_out_1,
  output data_out_0
);

  wire and_1_out, and_2_out, and_3_out, and_4_out;

  and and_1 (and_1_out, clock, CU, data_in_3);
  or or_1 (data_out_3, and_1_out, merge3);
  and and_2 (and_2_out, clock, CU, data_in_2);
  or or_2 (data_out_2, and_2_out, merge2);
  and and_3 (and_3_out, clock, CU, data_in_1);
  or or_3 (data_out_1, and_3_out, merge1);
  and and_4 (and_4_out, clock, CU, data_in_0);
  or or_4 (data_out_0, and_4_out, merge0);
endmodule

module modulo (
  input  clock,
  output out0,
  output out1,
  output out2,
  output out3,
  output out4,
  output out5,
  output out6,
  output out7,
  output out8,
  output out9,
  output out10,
  output out11,
  output out12,
  output out13,
  output out14,
  output out15,
  output out16,
  output out17,
  output out18,
  output out19
);

  wire and_1_out, d_ff_1_q, d_ff_1_qn, d_ff_2_q, d_ff_2_qn, d_ff_3_q, d_ff_3_qn, d_ff_4_q, d_ff_4_qn,
       d_ff_5_q, d_ff_5_qn, not_1_out, not_2_out, not_3_out, not_4_out, not_5_out, not_6_out, not_7_out,
       not_8_out, not_9_out, not_10_out, not_11_out, not_12_out, not_13_out, not_14_out, not_15_out,
       not_16_out, not_17_out, not_18_out, not_19_out, not_20_out, not_21_out, not_22_out, not_23_out,
       not_24_out, not_25_out, not_26_out, not_27_out, not_28_out, not_29_out, not_30_out, not_31_out,
       not_32_out, not_33_out, not_34_out, not_35_out, not_36_out, not_37_out, not_38_out, not_39_out,
       not_40_out, not_41_out, not_42_out, not_43_out, not_44_out, not_45_out, not_46_out, not_47_out,
       not_48_out, not_49_out, not_50_out, not_51_out, not_52_out, not_53_out, not_54_out, not_55_out,
       not_56_out, not_57_out, not_58_out, not_59_out, not_60_out;

  and and_1 (and_1_out, d_ff_5_q, d_ff_3_q);
  D_Flip_Flop d_ff_1 (.D(d_ff_1_qn), .clk(clock), .Q(d_ff_1_q), .Qn(d_ff_1_qn), .reset(and_1_out));  // open: preset
  D_Flip_Flop d_ff_2 (.D(d_ff_2_qn), .clk(d_ff_1_qn), .Q(d_ff_2_q), .Qn(d_ff_2_qn), .reset(and_1_out));  // open: preset
  D_Flip_Flop d_ff_3 (.D(d_ff_3_qn), .clk(d_ff_2_qn), .Q(d_ff_3_q), .Qn(d_ff_3_qn), .reset(and_1_out));  // open: preset
  D_Flip_Flop d_ff_4 (.D(d_ff_4_qn), .clk(d_ff_3_qn), .Q(d_ff_4_q), .Qn(d_ff_4_qn), .reset(and_1_out));  // open: preset
  D_Flip_Flop d_ff_5 (.D(d_ff_5_qn), .clk(d_ff_4_qn), .Q(d_ff_5_q), .Qn(d_ff_5_qn), .reset(and_1_out));  // open: preset
  not not_1 (not_1_out, d_ff_1_q);
  not not_2 (not_2_out, d_ff_2_q);
  not not_3 (not_3_out, d_ff_3_q);
  not not_4 (not_4_out, d_ff_4_q);
  not not_5 (not_5_out, d_ff_5_q);
  not not_6 (not_6_out, d_ff_2_q);
  not not_7 (not_7_out, d_ff_3_q);
  not not_8 (not_8_out, d_ff_4_q);
  not not_9 (not_9_out, d_ff_5_q);
  not not_10 (not_10_out, d_ff_1_q);
  not not_11 (not_11_out, d_ff_3_q);
  not not_12 (not_12_out, d_ff_4_q);
  not not_13 (not_13_out, d_ff_5_q);
  not not_14 (not_14_out, d_ff_3_q);
  not not_15 (not_15_out, d_ff_4_q);
  not not_16 (not_16_out, d_ff_5_q);
  not not_17 (not_17_out, d_ff_1_q);
  not not_18 (not_18_out, d_ff_2_q);
  not not_19 (not_19_out, d_ff_4_q);
  not not_20 (not_20_out, d_ff_5_q);
  not not_21 (not_21_out, d_ff_2_q);
  not not_22 (not_22_out, d_ff_4_q);
  not not_23 (not_23_out, d_ff_5_q);
  not not_24 (not_24_out, d_ff_1_q);
  not not_25 (not_25_out, d_ff_4_q);
  not not_26 (not_26_out, d_ff_5_q);
  not not_27 (not_27_out, d_ff_4_q);
  not not_28 (not_28_out, d_ff_5_q);
  not not_29 (not_29_out, d_ff_1_q);
  not not_30 (not_30_out, d_ff_2_q);
  not not_31 (not_31_out, d_ff_3_q);
  not not_32 (not_32_out, d_ff_5_q);
  not not_33 (not_33_out, d_ff_2_q);
  not not_34 (not_34_out, d_ff_3_q);
  not not_35 (not_35_out, d_ff_5_q);
  not not_36 (not_36_out, d_ff_1_q);
  not not_37 (not_37_out, d_ff_3_q);
  not not_38 (not_38_out, d_ff_5_q);
  not not_39 (not_39_out, d_ff_3_q);
  not not_40 (not_40_out, d_ff_5_q);
  not not_41 (not_41_out, d_ff_1_q);
  not not_42 (not_42_out, d_ff_2_q);
  not not_43 (not_43_out, d_ff_5_q);
  not not_44 (not_44_out, d_ff_2_q);
  not not_45 (not_45_out, d_ff_5_q);
  not not_46 (not_46_out, d_ff_1_q);
  not not_47 (not_47_out, d_ff_5_q);
  not not_48 (not_48_out, d_ff_5_q);
  not not_49 (not_49_out, d_ff_1_q);
  not not_50 (not_50_out, d_ff_2_q);
  not not_51 (not_51_out, d_ff_3_q);
  not not_52 (not_52_out, d_ff_4_q);
  not not_53 (not_53_out, d_ff_2_q);
  not not_54 (not_54_out, d_ff_3_q);
  not not_55 (not_55_out, d_ff_4_q);
  not not_56 (not_56_out, d_ff_1_q);
  not not_57 (not_57_out, d_ff_3_q);
  not not_58 (not_58_out, d_ff_4_q);
  not not_59 (not_59_out, d_ff_3_q);
  not not_60 (not_60_out, d_ff_4_q);
  and and_2 (out0, not_1_out, not_2_out, not_3_out, not_4_out, not_5_out);
  and and_3 (out1, d_ff_1_q, not_6_out, not_7_out, not_8_out, not_9_out);
  and and_4 (out2, not_10_out, d_ff_2_q, not_11_out, not_12_out, not_13_out);
  and and_5 (out3, d_ff_1_q, d_ff_2_q, not_14_out, not_15_out, not_16_out);
  and and_6 (out4, not_17_out, not_18_out, d_ff_3_q, not_19_out, not_20_out);
  and and_7 (out5, d_ff_1_q, not_21_out, d_ff_3_q, not_22_out, not_23_out);
  and and_8 (out6, not_24_out, d_ff_2_q, d_ff_3_q, not_25_out, not_26_out);
  and and_9 (out7, d_ff_1_q, d_ff_2_q, d_ff_3_q, not_27_out, not_28_out);
  and and_10 (out8, not_29_out, not_30_out, not_31_out, d_ff_4_q, not_32_out);
  and and_11 (out9, d_ff_1_q, not_33_out, not_34_out, d_ff_4_q, not_35_out);
  and and_12 (out10, not_36_out, d_ff_2_q, not_37_out, d_ff_4_q, not_38_out);
  and and_13 (out11, d_ff_1_q, d_ff_2_q, not_39_out, d_ff_4_q, not_40_out);
  and and_14 (out12, not_41_out, not_42_out, d_ff_3_q, d_ff_4_q, not_43_out);
  and and_15 (out13, d_ff_1_q, not_44_out, d_ff_3_q, d_ff_4_q, not_45_out);
  and and_16 (out14, not_46_out, d_ff_2_q, d_ff_3_q, d_ff_4_q, not_47_out);
  and and_17 (out15, d_ff_1_q, d_ff_2_q, d_ff_3_q, d_ff_4_q, not_48_out);
  and and_18 (out16, not_49_out, not_50_out, not_51_out, not_52_out, d_ff_5_q);
  and and_19 (out17, d_ff_1_q, not_53_out, not_54_out, not_55_out, d_ff_5_q);
  and and_20 (out18, not_56_out, d_ff_2_q, not_57_out, not_58_out, d_ff_5_q);
  and and_21 (out19, d_ff_1_q, d_ff_2_q, not_59_out, not_60_out, d_ff_5_q);
endmodule

module ALU_a6 (
  input  R3,
  input  R2,
  input  R1,
  input  R0,
  input  L3,
  input  L2,
  input  L1,
  input  L0,
  input  ADD_SUB,
  input  clock,
  output overflow,
  output zero,
  output negative,
  output out3,
  output out2,
  output out1,
  output out0
);

  wire addnagetive_out, addpositive_out, and_1_out, and_2_out, and_3_out, and_4_out, and_5_out, and_6_out,
       and_7_out, and_8_out, and_9_out, and_10_out, and_11_out, and_12_out, and_13_out, and_14_out,
       and_15_out, and_16_out, and_18_out, and_19_out, and_20_out, and_21_out, and_22_out, and_23_out,
       and_24_out, and_25_out, and_26_out, and_27_out, and_28_out, and_30_out, and_31_out, not_1_out,
       not_2_out, not_3_out, not_4_out, not_5_out, not_6_out, not_7_out, not_8_out, not_9_out, not_10_out,
       not_11_out, not_12_out, not_13_out, not_14_out, not_15_out, not_16_out, not_17_out, not_18_out,
       not_19_out, not_20_out, not_21_out, not_22_out, not_23_out, not_24_out, not_25_out, or_1_out,
       or_2_out, or_4_out, or_5_out, or_7_out, or_8_out, or_9_out, or_10_out, or_11_out, or_13_out,
       or_15_out, or_16_out, subnegpos_out, subposneg_out, xor_1_out, xor_2_out, xor_4_out, xor_5_out;

  and and_1 (and_1_out, L3, or_4_out);
  and and_2 (and_2_out, or_7_out, or_4_out);
  or or_1 (or_1_out, and_1_out, and_2_out, and_3_out);
  not not_1 (not_1_out, or_1_out);
  and and_3 (and_3_out, L3, or_7_out);
  or or_2 (or_2_out, L3, or_7_out, or_4_out);
  and and_4 (and_4_out, not_1_out, or_2_out);
  or or_3 (negative, and_4_out, and_5_out);
  and and_5 (and_5_out, L3, or_7_out, or_4_out);
  and and_6 (and_6_out, L2, or_9_out);
  and and_7 (and_7_out, or_8_out, or_9_out);
  or or_4 (or_4_out, and_6_out, and_7_out, and_8_out);
  and and_8 (and_8_out, L2, or_8_out);
  not not_2 (not_2_out, or_4_out);
  not not_3 (not_3_out, ADD_SUB);
  or or_5 (or_5_out, L2, or_8_out, or_9_out);
  and and_9 (and_9_out, not_2_out, or_5_out);
  or or_6 (out2, and_9_out, and_10_out);
  and and_10 (and_10_out, L2, or_8_out, or_9_out);
  and and_11 (and_11_out, not_3_out, R3);
  and and_12 (and_12_out, not_3_out, R2);
  or or_7 (or_7_out, and_11_out, and_19_out);
  and and_13 (and_13_out, not_3_out, R1);
  and and_14 (and_14_out, not_3_out, R0);
  or or_8 (or_8_out, and_12_out, and_23_out);
  and and_15 (and_15_out, L1, and_24_out);
  and and_16 (and_16_out, or_10_out, and_24_out);
  or or_9 (or_9_out, and_15_out, and_16_out, and_18_out);
  not not_4 (not_4_out, R3);
  // AND_Gate and_17 has open pins: in0=not_4_out, in1=and_22_out, out=open
  or or_10 (or_10_out, and_13_out, and_26_out);
  and and_18 (and_18_out, L1, or_10_out);
  not not_5 (not_5_out, or_9_out);
  xor xor_1 (xor_1_out, not_4_out, and_22_out);
  and and_19 (and_19_out, ADD_SUB, xor_1_out);
  or or_11 (or_11_out, L1, or_10_out, and_24_out);
  and and_20 (and_20_out, not_5_out, or_11_out);
  or or_12 (out1, and_20_out, and_21_out);
  and and_21 (and_21_out, L1, or_10_out, and_24_out);
  not not_6 (not_6_out, R2);
  and and_22 (and_22_out, not_6_out, and_25_out);
  and and_23 (and_23_out, ADD_SUB, xor_2_out);
  or or_13 (or_13_out, and_14_out, and_28_out);
  and and_24 (and_24_out, L0, or_13_out);
  xor xor_2 (xor_2_out, not_6_out, and_25_out);
  xor xor_3 (out0, L0, or_13_out);
  not not_7 (not_7_out, R1);
  and and_25 (and_25_out, not_7_out, and_27_out);
  and and_26 (and_26_out, ADD_SUB, xor_4_out);
  xor xor_4 (xor_4_out, not_7_out, and_27_out);
  not not_8 (not_8_out, R0);
  and and_27 (and_27_out, not_8_out, 1'b1);
  xor xor_5 (xor_5_out, not_8_out, 1'b1);
  and and_28 (and_28_out, ADD_SUB, xor_5_out);
  not not_9 (not_9_out, negative);
  not not_10 (not_10_out, out2);
  not not_11 (not_11_out, out1);
  not not_12 (not_12_out, out0);
  not not_13 (not_13_out, out2);
  not not_14 (not_14_out, out1);
  not not_15 (not_15_out, out0);
  not not_16 (not_16_out, L3);
  not not_17 (not_17_out, R3);
  not not_18 (not_18_out, ADD_SUB);
  not not_19 (not_19_out, negative);
  not not_20 (not_20_out, ADD_SUB);
  not not_21 (not_21_out, L3);
  and and_29 (zero, not_9_out, not_10_out, not_11_out, not_12_out);
  and and_30 (and_30_out, negative, not_13_out, not_14_out, not_15_out);
  and addpositive (addpositive_out, not_16_out, not_17_out, negative, not_18_out);
  and addnagetive (addnagetive_out, L3, R3, not_19_out, not_20_out);
  not not_22 (not_22_out, out2);
  not not_23 (not_23_out, out1);
  not not_24 (not_24_out, out0);
  not not_25 (not_25_out, L3);
  or or_14 (overflow, or_15_out, or_16_out);
  or or_15 (or_15_out, and_30_out, addpositive_out, addnagetive_out);
  and and_31 (and_31_out, negative, not_22_out, not_23_out, not_24_out);
  and subposneg (subposneg_out, not_25_out, R3, negative, ADD_SUB);
  and subnegpos (subnegpos_out, not_21_out, R3, negative, ADD_SUB);
  or or_16 (or_16_out, and_31_out, subposneg_out, subnegpos_out);

  assign out3 = negative;

  // Notes on the sheet:
  //   Add/Sub command
  //   L input
  //   A-out output
  //   R input
  //   2's complement
  //   overflow
  //   zero
  //   negative
  //   status output
endmodule

module STATUS (
  input  overflow,
  input  negtive,
  input  zero,
  input  clock,
  output negtive_out,
  output overflow_out,
  output zero_out
);

  D_Flip_Flop d_ff_1 (.D(overflow), .clk(clock), .Q(overflow_out));  // open: Qn, preset, reset
  D_Flip_Flop d_ff_2 (.D(negtive), .clk(clock), .Q(negtive_out));  // open: Qn, preset, reset
  D_Flip_Flop d_ff_3 (.D(zero), .clk(clock), .Q(zero_out));  // open: Qn, preset, reset
endmodule

module Display (
  input  in_1,
  input  in_2,
  input  in_3,
  input  in_4,
  output reg_1,
  output reg_2,
  output reg_3,
  output reg_4,
  output reg_5,
  output reg_6,
  output reg_7,
  output out_12
);

  wire and_1_out, and_2_out, and_3_out, and_4_out, and_5_out, and_6_out, and_7_out, and_8_out, and_9_out,
       and_10_out, and_11_out, and_12_out, and_13_out, and_14_out, and_15_out, and_16_out, not_1_out,
       not_2_out, not_3_out, not_4_out, not_5_out, not_6_out, not_7_out, not_8_out, not_9_out, not_10_out,
       not_11_out, not_12_out, not_13_out, not_14_out, not_15_out, not_16_out, not_17_out, not_18_out,
       not_19_out, not_20_out, not_21_out, not_22_out, not_23_out, not_24_out, not_25_out, not_26_out,
       not_27_out, not_28_out, not_29_out, not_30_out, not_31_out, not_32_out;

  not not_1 (not_1_out, in_1);
  not not_2 (not_2_out, in_2);
  not not_3 (not_3_out, in_3);
  not not_4 (not_4_out, in_4);
  not not_5 (not_5_out, in_1);
  not not_6 (not_6_out, in_2);
  not not_7 (not_7_out, in_3);
  not not_8 (not_8_out, in_1);
  not not_9 (not_9_out, in_2);
  not not_10 (not_10_out, in_4);
  not not_11 (not_11_out, in_1);
  not not_12 (not_12_out, in_2);
  not not_13 (not_13_out, in_1);
  not not_14 (not_14_out, in_3);
  not not_15 (not_15_out, in_4);
  not not_16 (not_16_out, in_1);
  not not_17 (not_17_out, in_3);
  not not_18 (not_18_out, in_1);
  not not_19 (not_19_out, in_4);
  not not_20 (not_20_out, in_1);
  not not_21 (not_21_out, in_2);
  not not_22 (not_22_out, in_3);
  not not_23 (not_23_out, in_4);
  not not_24 (not_24_out, in_2);
  not not_25 (not_25_out, in_3);
  not not_26 (not_26_out, in_2);
  not not_27 (not_27_out, in_3);
  not not_28 (not_28_out, in_4);
  not not_29 (not_29_out, in_3);
  not not_30 (not_30_out, in_4);
  not not_31 (not_31_out, in_2);
  not not_32 (not_32_out, in_4);
  and and_1 (and_1_out, not_1_out, not_2_out, not_3_out, not_4_out);
  and and_2 (and_2_out, not_5_out, not_6_out, not_7_out, in_4);
  and and_3 (and_3_out, not_8_out, not_9_out, in_3, not_10_out);
  and and_4 (and_4_out, not_11_out, not_12_out, in_3, in_4);
  and and_5 (and_5_out, not_13_out, in_2, not_14_out, not_15_out);
  and and_6 (and_6_out, not_16_out, in_2, not_17_out, in_4);
  and and_7 (and_7_out, not_18_out, in_2, in_3, not_19_out);
  and and_8 (and_8_out, not_20_out, in_2, in_3, in_4);
  and and_9 (and_9_out, in_1, not_21_out, not_22_out, not_23_out);
  and and_10 (and_10_out, in_1, not_24_out, not_25_out, in_4);
  and and_11 (and_11_out, in_1, not_26_out, in_3, in_4);
  and and_12 (and_12_out, in_1, in_2, not_27_out, not_28_out);
  and and_13 (and_13_out, in_1, in_2, not_29_out, in_4);
  and and_14 (and_14_out, in_1, in_2, in_3, not_30_out);
  and and_15 (and_15_out, in_1, in_2, in_3, in_4);
  and and_16 (and_16_out, in_1, not_31_out, in_3, not_32_out);
  or or_1 (out_12, and_11_out, and_12_out, and_16_out, and_13_out, and_14_out, and_15_out);
  or or_2 (reg_1, and_12_out, and_13_out, and_1_out, and_3_out, and_4_out, and_6_out, and_7_out, and_8_out, and_9_out, and_10_out, and_15_out, and_16_out);
  or or_3 (reg_2, and_14_out, and_1_out, and_9_out, and_5_out, and_15_out, and_6_out, and_7_out, and_10_out, and_16_out);
  or or_4 (reg_3, and_11_out, and_12_out, and_1_out, and_2_out, and_3_out, and_4_out, and_16_out, and_5_out, and_8_out, and_9_out, and_10_out, and_13_out, and_14_out);
  or or_5 (reg_4, and_12_out, and_13_out, and_3_out, and_4_out, and_5_out, and_6_out, and_7_out, and_9_out, and_10_out, and_14_out, and_15_out);
  or or_6 (reg_5, and_12_out, and_1_out, and_3_out, and_16_out, and_9_out, and_7_out, and_16_out);
  or or_7 (reg_6, and_6_out, and_11_out, and_13_out, and_1_out, and_2_out, and_4_out, and_5_out, and_7_out, and_8_out, and_9_out, and_10_out, and_14_out, and_15_out, and_16_out);
  or or_8 (reg_7, and_12_out, and_13_out, and_1_out, and_3_out, and_4_out, and_10_out, and_6_out, and_7_out, and_9_out, and_15_out, and_16_out);
endmodule
