// Logisim project a6.circ as structural Verilog: 1 circuit, main circuit main
module main (
  input  in_1,
  input  in_2,
  input  in_3,
  input  in_4,
  input  in_5,
  input  in_6,
  input  in_7,
  input  in_8,
  input  in_9,
  input  in_10,
  output out_11,
  output A_out,
  output out_13,
  output out_14,
  output out_15,
  output out_16,
  output out_17,
  output out_18
);

  wire and_1_out, and_2_out, and_3_out, and_4_out, and_6_out, and_7_out, and_8_out, and_9_out, and_10_out,
       and_11_out, and_12_out, and_13_out, and_14_out, and_15_out, and_16_out, and_18_out, and_20_out,
       and_21_out, and_22_out, clock_1_out, not_1_out, not_2_out, not_3_out, not_4_out, not_5_out, not_6_out,
       not_7_out, not_8_out, not_9_out, not_10_out, not_11_out, not_12_out, or_1_out, or_2_out, or_3_out,
       or_4_out, or_5_out, or_6_out, or_7_out, xor_2_out, xor_4_out, xor_6_out, xor_7_out, xor_9_out,
       xor_10_out, xor_11_out;

  xor xor_1 (out_13, in_2, or_2_out);
  and and_1 (and_1_out, in_2, or_2_out);
  xor xor_2 (xor_2_out, in_3, or_3_out);
  and and_2 (and_2_out, in_3, or_3_out);
  xor xor_3 (A_out, xor_2_out, and_1_out);
  and and_3 (and_3_out, and_1_out, xor_2_out);
  or or_1 (or_1_out, and_3_out, and_2_out);
  not not_1 (not_1_out, out_13);
  not not_2 (not_2_out, A_out);
  not not_3 (not_3_out, out_14);
  not not_4 (not_4_out, out_15);
  and and_4 (and_4_out, not_1_out, not_2_out, not_3_out, not_4_out);
  and and_5 (out_18, and_4_out, clock_1_out);
  not not_5 (not_5_out, in_1);
  and and_6 (and_6_out, in_6, not_5_out);
  or or_2 (or_2_out, and_6_out, and_12_out);
  and and_7 (and_7_out, in_7, not_6_out);
  not not_6 (not_6_out, in_1);
  or or_3 (or_3_out, and_7_out, and_15_out);
  xor xor_4 (xor_4_out, in_4, or_4_out);
  and and_8 (and_8_out, in_4, or_4_out);
  not not_7 (not_7_out, in_1);
  and and_9 (and_9_out, in_8, not_7_out);
  or or_4 (or_4_out, and_9_out, and_18_out);
  not not_8 (not_8_out, in_1);
  and and_10 (and_10_out, in_9, not_8_out);
  or or_5 (or_5_out, and_10_out, and_21_out);
  xor xor_5 (out_14, xor_4_out, or_1_out);
  and and_11 (and_11_out, or_1_out, xor_4_out);
  or or_6 (or_6_out, and_11_out, and_8_out);
  Clock clock_1 (.out(clock_1_out));
  not not_9 (not_9_out, in_6);
  and and_12 (and_12_out, xor_7_out, in_1);
  not not_10 (not_10_out, in_7);
  not not_11 (not_11_out, in_8);
  not not_12 (not_12_out, in_9);
  xor xor_6 (xor_6_out, in_5, or_5_out);
  and and_13 (and_13_out, in_5, or_5_out);
  xor xor_7 (xor_7_out, not_9_out, in_10);
  and and_14 (and_14_out, not_9_out, in_10);
  and and_15 (and_15_out, xor_9_out, in_1);
  xor xor_8 (out_15, xor_6_out, or_6_out);
  and and_16 (and_16_out, or_6_out, xor_6_out);
  or or_7 (or_7_out, and_16_out, and_13_out);
  and and_17 (out_16, clock_1_out, out_15);
  and and_18 (and_18_out, xor_10_out, in_1);
  and and_19 (out_17, clock_1_out, or_7_out);
  xor xor_9 (xor_9_out, not_10_out, and_14_out);
  and and_20 (and_20_out, not_10_out, and_14_out);
  and and_21 (and_21_out, xor_11_out, in_1);
  xor xor_10 (xor_10_out, not_11_out, and_20_out);
  and and_22 (and_22_out, not_11_out, and_20_out);
  xor xor_11 (xor_11_out, not_12_out, and_22_out);
  and and_23 (out_11, not_12_out, and_22_out);

  // Notes on the sheet:
  //   Ada Wang
  //   261027791
  //   A-out
  //   Left Input
  //   Add/Subtrat Command
  //   Status Output
  //   Bit 1: Zero
  //   Right Input
  //   A-out
  //   Status Output
  //   Bit 0: Negative
  //   A-out
  //   Status Output
  //   Bit 2: Overflow 
endmodule
